# Fritzing sketch c01_display_prototype (saved by Fritzing 0.7.4b)
breadboards: 1

parts:
  MAX1 = MAX7219
  LED1 = LED - 5mm [color="Green (560nm)" package="5 mm [THT]"]
  LED4 = LED - 5mm [color="Green (560nm)" package="5 mm [THT]"]
  LED3 = LED - 5mm [color="Red (633nm)" package="5 mm [THT]"]
  LED2 = LED - 5mm [color="Yellow (595nm)" package="5 mm [THT]"]
  LED5 = LED - 5mm [color="Yellow (595nm)" package="5 mm [THT]"]
  LED11 = LED - 5mm [color="Yellow (595nm)" package="5 mm [THT]"]
  LED8 = LED - 5mm [color="Yellow (595nm)" package="5 mm [THT]"]
  LED6 = LED - 5mm [color="Red (633nm)" package="5 mm [THT]"]
  LED9 = LED - 5mm [color="Red (633nm)" package="5 mm [THT]"]
  LED12 = LED - 5mm [color="Red (633nm)" package="5 mm [THT]"]
  LED7 = LED - 5mm [color="Green (560nm)" package="5 mm [THT]"]
  LED10 = LED - 5mm [color="Green (560nm)" package="5 mm [THT]"]
  C1 = Electrolytic Capacitor [capacitance=10µF package="100 mil [THT, electrolytic]"]
  C2 = Ceramic Capacitor [capacitance=100nF package="100 mil [THT, multilayer]"]
  R1 = Resistor [tolerance=±5% resistance=220 package=THT]
  R2 = Resistor [tolerance=±5% resistance=220 package=THT]
  Arduino1 = Arduino

nets:
  N1: MAX1.Ground, C1.-, C2.1, Arduino1.GND
  N2: MAX1.Iset, R1.Pin_1, R2.Pin_1
  N3: MAX1.V+, C1.+, C2.0, R1.Pin_0, R2.Pin_0, Arduino1.+5V
  N4: LED1.cathode, LED7.cathode
  N5: LED1.anode, LED4.anode, LED3.anode, LED2.anode, LED5.anode, LED6.anode
  N6: LED4.cathode, LED10.cathode
  N7: LED3.cathode, LED9.cathode
  N8: LED2.cathode, LED8.cathode
  N9: LED5.cathode, LED11.cathode
  N10: LED11.anode, LED8.anode, LED9.anode, LED12.anode, LED7.anode, LED10.anode
  N11: LED6.cathode, LED12.cathode

custom parts:
  MAX7219: Serially Interfaced, 8-Digit, LED Display Drivers
